# Fritzing sketch WRO (saved by Fritzing 0.9.3b)
breadboards: 1

parts:
  Part1 = Arduino Mega 2560 (Rev3)
  hc-sr1 = hc-sr04
  hc-sr2 = hc-sr04
  hc-sr3 = hc-sr04
  U1 = LM2596 step down module
  GY1 = GY-521 (MPU-6050) [form="♀ (female)" package=THT]
  M1 = DC Motor
  M2 = BTS7960
  hc-sr4 = hc-sr04
  hc-sr5 = hc-sr04
  hc-sr6 = hc-sr04
  U2 = TCM8240MD [package=tcm8240md]  # not connected
  SERVO3 = Tower Pro SG90 servo [part_number=101246]
  U3 = LM2596 step down module
  U4 = LM2596 step down module
  J2 = Basic Servo
  SERVO4 = Tower Pro SG90 servo [part_number=101246]
  SERVO5 = Tower Pro SG90 servo [part_number=101246]
  hc-sr7 = hc-sr04
  hc-sr8 = hc-sr04
  U6 = LIPO-2000mAh [package=lipo-2000]
  U7 = TCRT5000 [package=THT]

nets:
  N1: Part1.D21/SCL, GY1.pin3, GY1.pin6
  N2: Part1.D20/SDA, GY1.pin4, GY1.pin5
  N3: Part1.D19/RX1, U7.Pin_2
  N4: Part1.D13_PWM, M2.pin4
  N5: Part1.D12_PWM, M2.pin2
  N6: Part1.D11_PWM, M2.pin1
  N7: Part1.D10_PWM, M2.pin3
  N8: Part1.D9_PWM, hc-sr1.Trig
  N9: Part1.D8_PWM, hc-sr1.Echo
  VCC: Part1.5V, hc-sr1.VCC, hc-sr2.VCC, hc-sr3.VCC, GY1.pin1, M2.pin7, hc-sr4.VCC, hc-sr5.VCC, hc-sr6.VCC, hc-sr7.VCC, hc-sr8.VCC, U7.Pin_3
  GND: Part1.GND, hc-sr1.GND, hc-sr2.GND, hc-sr3.GND, U1.IN-, U1.OUT-, GY1.pin2, M2.pin8, M2.pin12, hc-sr4.GND, hc-sr5.GND, hc-sr6.GND, SERVO3.GND, U3.IN-, U3.OUT-, U4.IN-, U4.OUT-, SERVO4.GND, SERVO5.GND, hc-sr7.GND, hc-sr8.GND, U6.-, U7.Pin_4
  N10: Part1.VIN, U1.OUT+
  N11: Part1.D2_PWM, J2.pulse
  N12: Part1.D3_PWM, SERVO5.Signal
  N13: Part1.D4_PWM, SERVO4.Signal
  N14: Part1.D5_PWM, SERVO3.Signal
  N15: Part1.D6_PWM, hc-sr3.Echo
  N16: Part1.D7_PWM, hc-sr3.Trig
  N17: Part1.D28, hc-sr2.Echo
  N18: Part1.D30, hc-sr2.Trig
  N19: Part1.D37, hc-sr7.Trig
  N20: Part1.D39, hc-sr7.Echo
  N21: Part1.D41, hc-sr8.Trig
  N22: Part1.D43, hc-sr8.Echo
  N23: Part1.D44, hc-sr6.Echo
  N24: Part1.D46, hc-sr6.Trig
  N25: Part1.D48, hc-sr5.Echo
  N26: Part1.D50, hc-sr5.Trig
  N27: Part1.D52, hc-sr4.Trig
  N28: Part1.D53, hc-sr4.Echo
  N29: U1.IN+, M2.pin11, U3.IN+, U4.IN+, U6.+
  N30: M1.pin_1, M2.pin10
  N31: M1.pin_2, M2.pin9
  +5V: SERVO3.+5V, U3.OUT+, SERVO4.+5V, SERVO5.+5V

custom parts:
  LM2596 step down module: LM2596 DC-DC step down power supply module 3 A.
  GY-521 (MPU-6050): Placa GY-521 basada en conjunto de acelerómetro+giroscopios MPU-6050
  BTS7960: BTS7960 43A Peak Power H-Bridge PWM Motor Driver
  Tower Pro SG90 servo: Original file by John De Cristofaro http://www.adafruit.com/products/1449 Adafruit Feedback Servo (Small) Edited by: e-radionica.com 28/9/2015
  TCRT5000: TCRT5000 optical reflective sensor
